// Digital circuit CS303Project.dig as structural Verilog
module CS303Project (
  input  in_1,
  input  clk,
  output [6:0] out_3,
  output [15:0] out_4
);

  wire _0_out, _1_out, _2_out, _3_out, _4_out, _5_out, _6_out, _7_out, _8_out, _9_out, and_1_out, and_2_out,
       ID_2_out, PASS_2_out, u_encoder_da, u_mode_selector_ido, u_mode_selector_pwdo, u_shifter_pwd_led1,
       u_shifter_pwd_led2, u_shifter_pwd_led3, u_shifter_pwd_led4, u_shifter_pwd_match, u_timer_dis,
       u_timer_reset;
  wire [3:0] u_encoder_data, u_shifter_id0, u_shifter_id1;

  Button _1 (.out(_1_out));
  Button _4 (.out(_4_out));
  Button _7 (.out(_7_out));
  Button _2 (.out(_2_out));
  Button _5 (.out(_5_out));
  Button _8 (.out(_8_out));
  Button _0 (.out(_0_out));
  Button _3 (.out(_3_out));
  Button _6 (.out(_6_out));
  Button _9 (.out(_9_out));
  LED ID (.in(u_mode_selector_ido));
  LED PASS (.in(u_mode_selector_pwdo));
  Button ID_2 (.out(ID_2_out));
  Button PASS_2 (.out(PASS_2_out));
  mode_selector #(.applicationType("IVERILOG")) u_mode_selector (
    .ID(ID_2_out), .PWD(PASS_2_out), .DIS(u_timer_dis), .RESET(u_timer_reset), .CLK(clk), .RST(in_1),
    .IDO(u_mode_selector_ido), .PWDO(u_mode_selector_pwdo));
  encoder #(.applicationType("IVERILOG")) u_encoder (
    .P0(_0_out), .P1(_1_out), .P2(_2_out), .P3(_3_out), .P4(_4_out), .P5(_5_out), .P6(_6_out), .P7(_7_out),
    .P8(_8_out), .P9(_9_out), .CLK(clk), .RST(in_1), .DATA(u_encoder_data), .DA(u_encoder_da));
  ROM #(.AddrBits(7), .Bits(16)) Password (.A(out_3), .sel(1'b1), .D(out_4));
  timer #(.applicationType("IVERILOG")) u_timer (
    .START(u_shifter_pwd_led4), .CLK(clk), .RST(in_1), .RESET(u_timer_reset), .DIS(u_timer_dis));
  shifter #(.applicationType("IVERILOG")) u_shifter (
    .IN(u_encoder_data), .EN(u_mode_selector_ido), .DA(u_encoder_da), .CLK(clk), .RST(in_1),
    .ID1(u_shifter_id1), .ID0(u_shifter_id0), .HEX(out_3));
  shifter_pwd #(.applicationType("IVERILOG")) u_shifter_pwd (
    .DATAin(u_encoder_data), .PWDin(out_4), .EN(u_mode_selector_pwdo), .DA(u_encoder_da), .CLK(clk),
    .RST(in_1), .MATCH(u_shifter_pwd_match), .LED1(u_shifter_pwd_led1), .LED2(u_shifter_pwd_led2),
    .LED3(u_shifter_pwd_led3), .LED4(u_shifter_pwd_led4));
  Seven_Seg_Hex seven_seg_hex_1 (.d(u_shifter_id1), .dp(1'b0));
  Seven_Seg_Hex seven_seg_hex_2 (.d(u_shifter_id0), .dp(1'b0));
  LED led_1 (.in(u_shifter_pwd_led1));
  LED led_2 (.in(u_shifter_pwd_led2));
  and and_1 (and_1_out, u_shifter_pwd_match, u_shifter_pwd_led4);
  and and_2 (and_2_out, ~u_shifter_pwd_match, u_shifter_pwd_led4);  // And
  LED led_3 (.in(u_shifter_pwd_led3));
  LED led_4 (.in(u_shifter_pwd_led4));
  LED GRANTED (.in(and_1_out));
  LED DENIED (.in(and_2_out));

  // Notes on the sheet:
  //   clk: Hz: 100
  //   contents of Password (hex, n*v repeats v):
  //   1234,5678,33*ffff,1919,63*ffff
endmodule

/* Code of mode_selector:
module mode_selector (
  input ID, PWD, DIS, RESET, CLK, RST,
  output reg IDO, PWDO
);

  always @(posedge CLK or negedge RST) begin
    case ({RST, RESET})
      2'b00, 2'b11, 2'b01: begin
        IDO <= 1'b1;
        PWDO <= 1'b0;
      end
      2'b10: begin
        if (ID) begin
          IDO <= 1'b1;
          PWDO <= 1'b0;
        end
        else if (PWD) begin
          IDO <= 1'b0;
          PWDO <= 1'b1;
        end
      end
    endcase
  end

endmodule
*/

/* Code of encoder:
module encoder(
	input P0, P1, P2, P3, P4, P5, P6, P7, P8, P9,
	input CLK, RST,
	output reg [3:0] DATA,
	output reg DA);
	
	reg pressed;
	wire button;

	assign button = P0|P1|P2|P3|P4|P5|P6|P7|P8|P9;

	always @(posedge CLK, negedge RST) 
		if(~RST)
		begin
			pressed <= 0;
			DATA <= 4'b0000;
		end
		else
		begin
			if(button)
			begin
				if(~pressed)
				begin
					pressed <= 1'b1;
					DA <= 1'b1;
				end
				else
					DA <= 1'b0;
				if      (P0) DATA <= 4'b0000;
				else if (P1) DATA <= 4'b0001;
				else if (P2) DATA <= 4'b0010;
				else if (P3) DATA <= 4'b0011;
				else if (P4) DATA <= 4'b0100;
				else if (P5) DATA <= 4'b0101;
				else if (P6) DATA <= 4'b0110;
				else if (P7) DATA <= 4'b0111;
				else if (P8) DATA <= 4'b1000;
				else         DATA <= 4'b1001;
			end
			else
			begin
				pressed <= 1'b0;
				DA <= 1'b0;
			end				
		end			
endmodule
*/

/* Code of timer:
module timer (
  input START, CLK, RST,
  output reg RESET, DIS
);
  
  reg [8:0] counter;

  always @(posedge CLK or negedge RST) begin
    if (!RST) begin
      counter <= 9'b0;
      DIS <= 1'b0;
      RESET <= 1'b0;
    end
    else if (START) begin
      if (counter == 9'd300) begin
        counter <= 9'b0;
        DIS <= 1'b0;
        RESET <= 1'b1;
      end
      else begin
        counter <= counter + 9'd1;
        DIS <= 1'b1;
        RESET <= 1'b0;
      end
    end
    else begin
      counter <= 9'b0;
      DIS <= 1'b0;
      RESET <= 1'b0;
    end
  end

endmodule
*/

/* Code of shifter:
module shifter (
  input [3:0] IN,
  input EN, DA, CLK, RST,
  output reg [3:0] ID1, ID0,
  output reg [6:0] HEX
);

  reg [11:0] temp;

  always @(posedge CLK or negedge RST) begin
    if (~RST) begin
      ID1 <= 4'b0;
      ID0 <= 4'b0;
      HEX <= 7'b0;
      temp <= 12'b0;
    end
    else begin
      if (EN && DA) begin
        temp[11:4] <= temp[7:0];
        temp[3:0] <= IN;
      end

      ID1 <= temp[7:4];
      ID0 <= temp[3:0];
      HEX <= {ID1, ID0};
    end
  end

endmodule
*/

/* Code of shifter_pwd:
module shifter_pwd (
  input [3:0] DATAin,
  input [15:0] PWDin,
  input EN, DA, CLK, RST,
  output reg MATCH, LED1, LED2, LED3, LED4
);

  reg [15:0] pass;
  reg [1:0] led_index;

  always @(posedge CLK, negedge RST) begin
    if (~RST) begin
      MATCH <= 1'b0;
      LED1 <= 1'b0;
      LED2 <= 1'b0;
      LED3 <= 1'b0;
      LED4 <= 1'b0;
      led_index <= 2'b00;
      pass <= 16'b0;
    end
    else begin
      if (EN) begin
        if (DA) begin
          case (led_index)
            2'b00: begin
              LED1 <= 1'b1;
              pass[15:12] <= DATAin;
              led_index <= 2'b01;
            end
            2'b01: begin
              LED2 <= 1'b1;
              pass[11:8] <= DATAin;
              led_index <= 2'b10;
            end
            2'b10: begin
              LED3 <= 1'b1;
              pass[7:4] <= DATAin;
              led_index <= 2'b11;
            end
            2'b11: begin
              LED4 <= 1'b1;
              pass[3:0] <= DATAin;
            end
          endcase
        end
      end
      
      if (pass == PWDin)
        MATCH <= 1'b1;
      else
        MATCH <= 1'b0;
      
      if (!EN) begin
        MATCH <= 1'b0;
        LED1 <= 1'b0;
        LED2 <= 1'b0;
        LED3 <= 1'b0;
        LED4 <= 1'b0;
	led_index <= 2'b00;
	pass <= 16'b0;
      end
    end
  end
endmodule
*/
