// Digital circuit mode_selector.dig as structural Verilog
module mode_selector (
  input  ID,
  input  PWD,
  input  DIS,
  input  RESET,
  input  CLK,
  input  RST,
  output IDO,
  output PWDO
);

  External #(.applicationType("IVERILOG")) u_external_1 (
    .ID(ID), .PWD(PWD), .DIS(DIS), .RESET(RESET), .CLK(CLK), .RST(RST), .IDO(IDO), .PWD0(PWDO));
endmodule

/* Code of External:
module mode_selector(
    input ID,
    input PWD,
    input DIS,
    input RESET,
    input CLK,
    input RST,
    output reg IDO,
    output reg PWDO
);

reg [1:0] mode_reg;

always @(posedge CLK, negedge RST) begin
    if (~RST) begin
        mode_reg <= 2'b00;
        IDO <= 1'b0;
        PWDO <= 1'b0;
    end
    else begin
        if (RESET) begin
            mode_reg <= 2'b00;
            IDO <= 1'b0;
            PWDO <= 1'b0;
        end
        else begin
            case (mode_reg)
                2'b00: begin
                    if (ID) begin
                        mode_reg <= 2'b01;
                        IDO <= 1'b1;
                        PWDO <= 1'b0;
                    end
                    else if (PWD) begin
                        mode_reg <= 2'b10;
                        IDO <= 1'b0;
                        PWDO <= 1'b1;
                    end
                    else begin
                        mode_reg <= 2'b00;
                        IDO <= 1'b0;
                        PWDO <= 1'b0;
                    end
                end
                2'b01: begin
                    if (DIS) begin
                        mode_reg <= 2'b00;
                        IDO <= 1'b0;
                        PWDO <= 1'b0;
                    end
                end
                2'b10: begin
                    if (DIS) begin
                        mode_reg <= 2'b00;
                        IDO <= 1'b0;
                        PWDO <= 1'b0;
                    end
                end
            endcase
        end
    end
end

endmodule
*/
