// Digital circuit shifter.dig as structural Verilog
module shifter (
  input  [3:0] IN,
  input  EN,
  input  DA,
  input  CLK,
  input  RST,
  output [3:0] ID1,
  output [3:0] ID0,
  output [6:0] HEX
);

  shifter #(.applicationType("IVERILOG")) u_shifter (
    .IN(IN), .EN(EN), .DA(DA), .CLK(CLK), .RST(RST), .ID1(ID1), .ID0(ID0), .HEX(HEX));
endmodule

/* Code of shifter:
module shifter(
    input [3:0] IN,
    input EN,
    input DA,
    input CLK,
    input RST,
    output reg [3:0] ID1,
    output reg [3:0] ID0,
    output reg [6:0] HEX
);

reg [3:0] id1_reg;
reg [3:0] id0_reg;
reg [6:0] hex_reg;

always @(posedge CLK, negedge RST) begin
    if (~RST) begin
        id1_reg <= 4'b0000;
        id0_reg <= 4'b0000;
        hex_reg <= 7'b0000000;
    end
    else if (EN) begin
        if (DA) begin
            id1_reg <= id0_reg;
            id0_reg <= IN;
        end
        hex_reg <= {id1_reg, id0_reg};
    end
end

assign ID1 = id1_reg;
assign ID0 = id0_reg;
assign HEX = hex_reg;

endmodule
*/
