// Digital circuit shifter_pwd.dig as structural Verilog
module shifter_pwd (
  input  [15:0] DATA_in,
  input  [99:0] PWD_in,
  input  EN,
  input  DA,
  input  CLK,
  input  RST,
  output MATCH,
  output LED1,
  output LED2,
  output LED3,
  output LED4
);

  shifter_pwd #(.applicationType("IVERILOG")) u_shifter_pwd (
    .DATAin(DATA_in), .PWDin(PWD_in), .EN(DA), .DA(EN), .CLK(CLK), .RST(RST), .MATCH(MATCH), .LED1(LED1),
    .LED2(LED2), .LED3(LED3), .LED4(LED4));
  // Pins of 4 and 16 bits meet at DATA_in
  // Pins of 16 and 100 bits meet at PWD_in
endmodule

/* Code of shifter_pwd:
module shifter_pwd(
    input [15:0] DATAin,
    input [99:0] PWDin,
    input EN,
    input DA,
    input CLK,
    input RST,
    output reg MATCH,
    output reg LED1,
    output reg LED2,
    output reg LED3,
    output reg LED4
);

reg [3:0] code_reg [0:3];
reg [3:0] user_code_reg [0:3];
reg [5:0] led_reg;
reg [5:0] timer_reg;
reg match_reg;

integer i;

always @(posedge CLK, negedge RST) begin
    if (~RST) begin
        for (i = 0; i < 4; i = i + 1) begin
            code_reg[i] <= 4'b0000;
            user_code_reg[i] <= 4'b0000;
        end
        led_reg <= 6'b000000;
        timer_reg <= 6'b000000;
        match_reg <= 1'b0;
    end
    else if (EN) begin
        if (DA) begin
            for (i = 0; i < 3; i = i + 1) begin
                code_reg[i] <= code_reg[i+1];
                user_code_reg[i] <= user_code_reg[i+1];
            end
            code_reg[3] <= DATAin[3:0];
            user_code_reg[3] <= PWDin[(DA ? 10 : 0) + DATAin[3:0]];
            led_reg <= led_reg + 6'b000001;
            if (led_reg == 6'b111111) begin
                match_reg <= (code_reg == user_code_reg);
                led_reg <= 6'b000000;
                timer_reg <= 6'b000000;
            end
            else begin
                timer_reg <= timer_reg + 6'b000001;
                if (timer_reg == 6'b111111) begin
                    led_reg <= 6'b000000;
                    timer_reg <= 6'b000000;
                end
            end
        end
    end
end

assign MATCH = match_reg;
assign LED1 = led_reg[5];
assign LED2 = led_reg[4];
assign LED3 = led_reg3];
assign LED4 = led_reg[2];

endmodule
*/
