// Digital circuit timer.dig as structural Verilog
module timer (
  input  START,
  input  CLK,
  input  RST,
  output RESET,
  output DIS
);

  timer #(.applicationType("IVERILOG")) u_timer (.RST(RST), .START(START), .CLK(CLK), .DIS(DIS), .RESET(RESET));
endmodule

/* Code of timer:
module timer(
    input START,
    input CLK,
    input RST,
    output reg RESET,
    output reg DIS
);

reg [5:0] count_reg;

always @(posedge CLK, negedge RST) begin
    if (~RST) begin
        count_reg <= 6'b000000;
        RESET <= 1'b0;
        DIS <= 1'b1;
    end
    else if (START) begin
        count_reg <= count_reg + 6'b000001;
        if (count_reg == 6'b111111) begin
            RESET <= 1'b1;
            DIS <= 1'b0;
        end
    end
    else begin
        count_reg <= 6'b000000;
        RESET <= 1'b0;
        DIS <= 1'b1;
    end
end

endmodule
*/
