// Digital circuit abs.dig as structural Verilog
module abs (
  input  [3:0] in,
  output [3:0] out,
  output sign
);

  wire [2:0] xor_1_out;

  xor xor_1 (xor_1_out[0], in[0], in[3]);
  xor xor_2 (xor_1_out[2], in[3], in[2]);
  xor xor_3 (xor_1_out[1], in[1], in[3]);
  Add #(.Bits(3)) add_1 (.a(xor_1_out), .b(3'b000), .c_i(in[3]), .s(out[2:0]));  // open: c_o

  assign out[3] = in[3];
  assign sign = in[3];
endmodule
