// Digital circuit core.dig as structural Verilog
module core (
  input  A0,
  input  A1,
  input  B0,
  input  B1,
  output [3:0] M
);

  wire and_1_out, and_5_out;
  wire [2:0] and_3_out, and_6_out;
  wire [2:1] add_1_s;

  and and_1 (and_1_out, A1, B0);
  buf and_2 (M[3], B0);  // And open: In_1
  and and_3 (and_3_out[0], A0, B1);
  and and_4 (and_3_out[0], A1, B1);
  and and_5 (and_5_out, and_1_out, and_3_out[0]);
  and and_6 (and_6_out[0], and_5_out, M[3]);
  // And and_7 has open pins: In_1=and_5_out, In_2=M[3], out=open
  Add #(.Bits(3)) add_1 (.a(and_3_out), .b(and_6_out), .c_i(M[3]), .s({add_1_s, M[3]}), .c_o(M[3]));
  // Pins of 1 and 3 bits meet at {add_1_s, M[3]}
  // Pins of 1 and 3 bits meet at and_3_out
  // Pins of 1 and 3 bits meet at and_6_out

  assign M[2:0] = {3{M[3]}};
endmodule
