// Digital circuit lab1b.dig as structural Verilog
module lab1b (
  input  in_1,
  input  in_2,
  input  in_3,
  input  in_4,
  input  [3:0] in,
  output [5:0] out
);

  wire [3:0] unsignedbcd6_1_p1, unsignedbcd6_1_p2, unsignedbcd_1_p1, unsignedbcd_1_p3;

  Seven_Seg_Hex seven_seg_hex_1 (.d(unsignedbcd_1_p1), .dp(1'b0));
  Seven_Seg_Hex seven_seg_hex_2 (.d(unsignedbcd_1_p3), .dp(1'b0));
  // unsignedBCD unsignedbcd_1: pin names not known; wires that end beside it: unsignedbcd_1_p1, {in_1, in_2, in_3, in_4}, unsignedbcd_1_p3
  Seven_Seg_Hex seven_seg_hex_3 (.d(unsignedbcd6_1_p1), .dp(1'b0));
  Seven_Seg_Hex seven_seg_hex_4 (.d(unsignedbcd6_1_p2), .dp(1'b0));
  // unsignedBCD6 unsignedbcd6_1: pin names not known; wires that end beside it: unsignedbcd6_1_p1, unsignedbcd6_1_p2
  Add #(.Bits(5)) add_1 (.a({in, 1'b0}), .b({1'b0, in}), .c_i(1'b0), .s(out[4:0]), .c_o(out[5]));
  // Pins of 1 and 4 bits meet at in
  // Pins of 1 and 6 bits meet at out

  // Notes on the sheet:
  //   3x
  //   =
endmodule
