// Digital circuit inlab_4.dig as structural Verilog
module inlab_4 (
  input  _100_Hz,
  input  RESET
);

  wire BD_out, BU_out, cntdecud_1_p1, cntdecud_1_p2, cntdecud_1_p6, cntdecud_1_p7, cntdecud_2_p1,
       cntdecud_2_p2, d_ff_1_q, d_ff_2_q;
  wire [3:0] cntdecud_1_p5, cntdecud_2_p5;

  D_FF d_ff_1 (.D(BU_out), .C(_100_Hz), .Q(d_ff_1_q));  // open: nQ
  D_FF d_ff_2 (.D(BD_out), .C(_100_Hz), .Q(d_ff_2_q));  // open: nQ
  // cntDECud cntdecud_1: pin names not known; wires that end beside it: cntdecud_1_p1, cntdecud_1_p2, _100_Hz, RESET, cntdecud_1_p5, cntdecud_1_p6, cntdecud_1_p7
  // cntDECud cntdecud_2: pin names not known; wires that end beside it: cntdecud_2_p1, cntdecud_2_p2, _100_Hz, RESET, cntdecud_2_p5
  Button BU (.out(BU_out));
  xor xor_1 (cntdecud_1_p1, d_ff_1_q, _100_Hz);
  Button BD (.out(BD_out));
  and and_1 (cntdecud_2_p1, cntdecud_1_p1, cntdecud_1_p7);
  and and_2 (cntdecud_2_p2, cntdecud_1_p6, cntdecud_1_p2);
  xor xor_2 (cntdecud_1_p2, d_ff_2_q, _100_Hz);
  Seven_Seg_Hex seven_seg_hex_1 (.d(cntdecud_2_p5), .dp(1'b0));
  Seven_Seg_Hex seven_seg_hex_2 (.d(cntdecud_1_p5), .dp(1'b0));

  // Notes on the sheet:
  //   _100_Hz: Hz: 20
endmodule
