// Digital circuit lab_2.dig as structural Verilog
module lab_2 (
  input  MSB__A,
  input  B,
  input  C,
  input  LSB__D,
  input  MSB__A_2,
  input  B_2,
  input  C_2,
  input  LSB__D_2
);

  wire add_1_c_o, add_1_s, add_2_c_o, add_2_s, add_3_s, add_4_s, add_5_s, and_1_out, and_2_out, and_3_out,
       and_4_out, and_5_out, and_6_out, and_7_out, and_8_out, and_9_out, and_10_out, and_11_out, and_12_out,
       not_1_out, not_2_out, not_3_out, not_4_out, not_5_out, not_6_out, not_7_out, not_8_out, or_1_out,
       or_2_out, or_3_out, or_4_out, or_5_out, or_6_out, xor_1_out, xor_2_out, xor_3_out, xor_4_out;

  not not_1 (not_1_out, MSB__A);
  not not_2 (not_2_out, B);
  not not_3 (not_3_out, C);
  not not_4 (not_4_out, LSB__D);
  not not_5 (not_5_out, MSB__A_2);
  not not_6 (not_6_out, B_2);
  not not_7 (not_7_out, C_2);
  not not_8 (not_8_out, LSB__D_2);
  and and_1 (and_1_out, not_1_out, B);
  and and_2 (and_2_out, not_2_out, C);
  and and_3 (and_3_out, not_3_out, LSB__D);
  and and_4 (and_4_out, not_5_out, B_2);
  and and_5 (and_5_out, not_6_out, C_2);
  and and_6 (and_6_out, not_7_out, LSB__D_2);
  and and_7 (and_7_out, MSB__A, not_2_out);
  and and_8 (and_8_out, B, not_3_out);
  and and_9 (and_9_out, not_3_out, not_4_out);
  and and_10 (and_10_out, MSB__A_2, not_6_out);
  and and_11 (and_11_out, B_2, not_7_out);
  and and_12 (and_12_out, not_7_out, not_8_out);
  or or_1 (or_1_out, and_1_out, and_7_out);
  or or_2 (or_2_out, and_2_out, and_8_out);
  or or_3 (or_3_out, and_3_out, and_9_out);
  or or_4 (or_4_out, and_4_out, and_10_out);
  or or_5 (or_5_out, and_5_out, and_11_out);
  or or_6 (or_6_out, and_6_out, and_12_out);
  LED X_1__MSB (.in(MSB__A));
  LED Y_1 (.in(or_1_out));
  LED Z_1 (.in(or_2_out));
  LED T_2__LSB (.in(or_3_out));
  LED X_2__MSB (.in(MSB__A_2));
  LED Y_2 (.in(or_4_out));
  LED Z_2 (.in(or_5_out));
  LED T_2__LSB_2 (.in(or_6_out));
  xor xor_1 (xor_1_out, or_2_out, or_5_out);
  xor xor_2 (xor_2_out, or_1_out, or_4_out);
  xor xor_3 (xor_3_out, or_3_out, or_6_out);
  xor xor_4 (xor_4_out, MSB__A, MSB__A_2);
  Add add_1 (.a(xor_4_out), .b(xor_2_out), .c_i(1'b0), .s(add_1_s), .c_o(add_1_c_o));
  Add add_2 (.a(xor_1_out), .b(xor_3_out), .c_i(1'b0), .s(add_2_s), .c_o(add_2_c_o));
  Add add_3 (.a(add_1_s), .b(add_1_c_o), .c_i(1'b0), .s(add_3_s));  // open: c_o
  Add add_4 (.a(add_2_s), .b(add_2_c_o), .c_i(1'b0), .s(add_4_s));  // open: c_o
  Add add_5 (.a(add_3_s), .b(add_4_s), .c_i(1'b0), .s(add_5_s));  // open: c_o
  LED led_1 (.in(add_5_s));

  // Notes on the sheet:
  //   X = A
  //   Y = (A AND (NOT B)) OR ((NOT A) AND B)
  //   Z = (B AND (NOT C)) OR ((NOT B) AND C)
  //   T = (C AND (NOT D)) OR ((NOT C) AND D)
  //   XOR1: X_1 ⊕ X_2 -> X1
  //   XOR2: Y_1 ⊕ Y_2 -> X2
  //   XOR3: Z_1 ⊕ Z_2 -> X3
  //   XOR4: T_1 ⊕ T_2 -> X4
  //   XOR_2
  //   XOR_3
  //   XOR_1
  //   XOR_4
endmodule
