// Digital circuit statemachine.dig as structural Verilog
module statemachine (
  input  A,
  input  B,
  input  CLK,
  output OUT
);

  wire and_1_out, and_2_out, and_3_out, and_4_out, d_ff_1_q, d_ff_2_nq, d_ff_2_q, not_1_out, or_1_out,
       or_2_out;

  not not_1 (not_1_out, A);
  D_FF d_ff_1 (.D(or_1_out), .C(CLK), .Q(d_ff_1_q));  // open: nQ
  D_FF d_ff_2 (.D(or_2_out), .C(CLK), .Q(d_ff_2_q), .nQ(d_ff_2_nq));
  and and_1 (and_1_out, d_ff_2_q, B);
  and and_2 (and_2_out, A, d_ff_1_q);
  and and_3 (and_3_out, B, not_1_out);
  and and_4 (and_4_out, A, d_ff_1_q);
  or or_1 (or_1_out, and_1_out, and_2_out);
  or or_2 (or_2_out, and_3_out, and_4_out);
  and and_5 (OUT, d_ff_1_q, d_ff_2_nq, not_1_out);
endmodule
