// Digital circuit tallycounter_28368.dig as structural Verilog
module tallycounter_28368 (
  input  _100_Hz,
  input  RESET
);

  wire and_1_out, BD_out, BU_out, cntdecud_1_p2, cntdecud_1_p6, cntdecud_1_p7, cntdecud_2_p1, cntdecud_2_p2,
       d_ff_1_nq, d_ff_2_nq;
  wire [3:0] cntdecud_1_p5, cntdecud_2_p5;

  D_FF d_ff_1 (.D(BU_out), .C(_100_Hz), .nQ(d_ff_1_nq));  // open: Q
  D_FF d_ff_2 (.D(BD_out), .C(_100_Hz), .nQ(d_ff_2_nq));  // open: Q
  and and_1 (and_1_out, BU_out, d_ff_1_nq);
  // cntDECud cntdecud_1: pin names not known; wires that end beside it: and_1_out, cntdecud_1_p2, _100_Hz, RESET, cntdecud_1_p5, cntdecud_1_p6, cntdecud_1_p7
  // cntDECud cntdecud_2: pin names not known; wires that end beside it: cntdecud_2_p1, cntdecud_2_p2, _100_Hz, RESET, cntdecud_2_p5
  Button BU (.out(BU_out));
  and and_2 (cntdecud_2_p1, and_1_out, cntdecud_1_p7);
  and and_3 (cntdecud_2_p2, cntdecud_1_p6, cntdecud_1_p2);
  Button BD (.out(BD_out));
  and and_4 (cntdecud_1_p2, BD_out, d_ff_2_nq);
  Seven_Seg_Hex seven_seg_hex_1 (.d(cntdecud_2_p5), .dp(1'b0));
  Seven_Seg_Hex seven_seg_hex_2 (.d(cntdecud_1_p5), .dp(1'b0));

  // Notes on the sheet:
  //   _100_Hz: Hz: 100
endmodule
