// Digital circuit upcounter.dig as structural Verilog
module upcounter (
  input  EN,
  input  LOAD,
  input  [3:0] IN,
  input  CLK,
  output [3:0] CNT
);

  wire add_1_c_o, and_4_out, d_ff_as_1_nq, d_ff_as_2_nq, d_ff_as_3_nq, d_ff_as_4_nq, multiplexer_1_out,
       multiplexer_2_out, multiplexer_3_out, multiplexer_4_out, not_1_out;
  wire [0:0] and_1_out, and_2_out, and_3_out;
  wire [3:0] d_ff_as_1_q;

  and and_1 (and_1_out[0], d_ff_as_1_q[0], EN);
  and and_2 (and_2_out[0], d_ff_as_1_q[1], and_1_out[0]);
  and and_3 (and_3_out[0], d_ff_as_1_q[2], and_2_out[0]);
  Multiplexer #(.Selector_Bits(2)) multiplexer_1 (
    .sel({LOAD, EN}), .in_0(d_ff_as_1_q[0]), .in_1(d_ff_as_1_nq), .in_2(CNT[0]), .in_3(CNT[0]),
    .out(multiplexer_1_out));
  Multiplexer #(.Selector_Bits(2)) multiplexer_2 (
    .sel({LOAD, and_1_out[0]}), .in_0(d_ff_as_1_q[1]), .in_1(d_ff_as_2_nq), .in_2(CNT[1]), .in_3(CNT[1]),
    .out(multiplexer_2_out));
  Multiplexer #(.Selector_Bits(2)) multiplexer_3 (
    .sel({LOAD, and_2_out[0]}), .in_0(d_ff_as_1_q[2]), .in_1(d_ff_as_3_nq), .in_2(CNT[2]), .in_3(CNT[2]),
    .out(multiplexer_3_out));
  Multiplexer #(.Selector_Bits(2)) multiplexer_4 (
    .sel({LOAD, and_3_out[0]}), .in_0(d_ff_as_1_q[3]), .in_1(d_ff_as_4_nq), .in_2(CNT[3]), .in_3(CNT[3]),
    .out(multiplexer_4_out));
  D_FF_AS d_ff_as_1 (
    .Set(1'b0), .D(multiplexer_1_out), .C(CLK), .Clr(and_4_out), .Q(d_ff_as_1_q[0]), .nQ(d_ff_as_1_nq));
  D_FF_AS d_ff_as_2 (
    .Set(1'b0), .D(multiplexer_2_out), .C(CLK), .Clr(and_4_out), .Q(d_ff_as_1_q[1]), .nQ(d_ff_as_2_nq));
  D_FF_AS d_ff_as_3 (
    .Set(1'b0), .D(multiplexer_3_out), .C(CLK), .Clr(and_4_out), .Q(d_ff_as_1_q[2]), .nQ(d_ff_as_3_nq));
  D_FF_AS d_ff_as_4 (
    .Set(1'b0), .D(multiplexer_4_out), .C(CLK), .Clr(and_4_out), .Q(d_ff_as_1_q[3]), .nQ(d_ff_as_4_nq));
  Add #(.Bits(4)) add_1 (.a(d_ff_as_1_q), .b(4'b0101), .c_i(1'b0), .s(CNT), .c_o(add_1_c_o));
  not not_1 (not_1_out, CNT[1]);
  and and_4 (and_4_out, CNT[0], not_1_out, CNT[2], CNT[3]);
  // And and_5 has open pins: In_1=d_ff_as_1_nq, In_2=d_ff_as_3_nq, In_3=d_ff_as_2_nq, In_4=d_ff_as_4_nq, out=open
  // also tied to GND on the sheet: add_1_c_o
endmodule
